// Logisim project beta_machine_3.0.circ as structural Verilog: 6 circuits, main circuit ALU_x32
module main (
  output [31:0] out_1
);

  wire BSEL, button_1_out, clock_1_out, WERF;
  wire [1:0] control_logic_x32_1_out_2, control_logic_x32_1_out_2_3;
  wire [3:0] ALUFN;
  wire [3:2] control_logic_x32_1_out_2_2;
  wire [31:0] adder_1_out, instruction_memory_x32_1_out_2, multiplexer_1_out, register_1_q,
       register_file_1_out_6, register_file_1_out_7;

  Adder #(.width(32)) adder_1 (.a(register_1_q), .b(32'h4), .out(adder_1_out));  // open: cin, cout
  Clock clock_1 (.out(clock_1_out));
  instruction_memory_x32 instruction_memory_x32_1 (.in_1(register_1_q), .out_2(instruction_memory_x32_1_out_2));
  Register #(.width(32)) register_1 (
    .D(adder_1_out), .Q(register_1_q), .clk(clock_1_out), .clr(button_1_out));  // open: en
  Button button_1 (.out(button_1_out));
  control_logic_x32 control_logic_x32_1 (
    .in_1(instruction_memory_x32_1_out_2[31:26]),
    .out_2({ALUFN, WERF, BSEL, control_logic_x32_1_out_2_3, control_logic_x32_1_out_2_2, control_logic_x32_1_out_2}));
  register_file register_file_1 (
    .WA(instruction_memory_x32_1_out_2[25:21]), .RA1(instruction_memory_x32_1_out_2[20:16]),
    .RA2(instruction_memory_x32_1_out_2[15:11]), .WE(WERF), .in_3(out_1), .out_6(register_file_1_out_6),
    .out_7(register_file_1_out_7));
  ALU_x32 alu_x32_1 (.ALUFN(ALUFN), .A(register_file_1_out_6), .B(multiplexer_1_out), .Output(out_1));
  Multiplexer #(.width(32), .enable("false")) multiplexer_1 (
    .in0({{16{1'b0}}, instruction_memory_x32_1_out_2[15:0]}), .in1(register_file_1_out_7),
    .out(multiplexer_1_out), .sel(BSEL));

  // Notes on the sheet:
  //   Arthur LOUIS - S191230
endmodule

module control_logic_x32 (
  input  [5:0] in_1,
  output [11:0] out_2
);

  ROM #(.addrWidth(6), .dataWidth(12)) rom_1 (.addr(in_1), .data(out_2));  // open: sel

  // Notes on the sheet:
  //   contents of rom_1 (hex, n*v repeats v):
  //   32*0 c0 1c0 2c0 3c0 7c0 8c0 9c0 0 4c0 5c0 6c0 0 ac0 bc0 cc0 0 80 180 280 380 780 880 980 0 480 580
  //   680 0 a80 b80 c80
endmodule

module ALU_x32 (
  input  [31:0] A,
  input  [31:0] B,
  input  [3:0] ALUFN,
  output [31:0] Output
);

  wire [31:0] adder_1_out, and_1_out, comparator_x32_1_equal, comparator_x32_1_lower_or_equal,
       comparator_x32_1_smaller, divider_1_out, multiplier_1_out, or_1_out, shifter_1_out, shifter_2_out,
       shifter_3_out, subtractor_1_out, xor_1_out;

  Divider #(.width(32)) divider_1 (.a(A), .b(B), .out(divider_1_out));  // open: upper, rem
  Multiplier #(.width(32)) multiplier_1 (.a(A), .b(B), .out(multiplier_1_out));  // open: cin, cout
  Subtractor #(.width(32)) subtractor_1 (.a(A), .b(B), .out(subtractor_1_out));  // open: bin, bout
  Adder #(.width(32)) adder_1 (.a(A), .b(B), .out(adder_1_out));  // open: cin, cout
  assign and_1_out = A & B;  // AND_Gate and_1, 32 bits wide
  comparator_x32 comparator_x32_1 (
    .in_1(A), .in_2(B), .Equal(comparator_x32_1_equal), .Smaller(comparator_x32_1_smaller),
    .Lower_or_equal(comparator_x32_1_lower_or_equal));  // open: Greater, Greater_or_equal
  assign xor_1_out = A ^ B;  // XOR_Gate xor_1, 32 bits wide
  assign or_1_out = A | B;  // OR_Gate or_1, 32 bits wide
  Multiplexer #(.select(4), .width(32), .enable("false")) multiplexer_1 (
    .in0(adder_1_out), .in1(subtractor_1_out), .in2(multiplier_1_out), .in3(divider_1_out), .in4(and_1_out),
    .in5(or_1_out), .in6(xor_1_out), .in7(comparator_x32_1_equal), .in8(comparator_x32_1_smaller),
    .in9(comparator_x32_1_lower_or_equal), .in10(shifter_3_out), .in11(shifter_2_out), .in12(shifter_1_out),
    .in13({32{1'b0}}), .in14({32{1'b0}}), .in15({32{1'b0}}), .out(Output), .sel(ALUFN));
  Shifter #(.width(32), .shift("ar")) shifter_1 (.in(A), .\dist (B[4:0]), .out(shifter_1_out));
  Shifter #(.width(32), .shift("lr")) shifter_2 (.in(A), .\dist (B[4:0]), .out(shifter_2_out));
  Shifter #(.width(32)) shifter_3 (.in(A), .\dist (B[4:0]), .out(shifter_3_out));

  // Notes on the sheet:
  //   Input ALUFN : Choose function
  //   Input A
  //   Input B
endmodule

module register_file (
  input  WE,
  input  [4:0] WA,
  input  [31:0] in_3,
  input  [4:0] RA1,
  input  [4:0] RA2,
  output [31:0] out_6,
  output [31:0] out_7
);

  wire clock_1_out, demultiplexer_1_out0, demultiplexer_1_out1, demultiplexer_1_out2, demultiplexer_1_out3,
       demultiplexer_1_out4, demultiplexer_1_out29, demultiplexer_1_out30;
  wire [31:0] r4_q, register_1_q, register_2_q, register_3_q, register_4_q, register_5_q, register_6_q;

  Clock clock_1 (.out(clock_1_out));
  Register #(.width(32)) register_1 (
    .D(in_3), .en(demultiplexer_1_out0), .Q(register_1_q), .clk(clock_1_out));  // open: clr
  Register #(.width(32)) register_2 (
    .D(in_3), .en(demultiplexer_1_out1), .Q(register_2_q), .clk(clock_1_out));  // open: clr
  Demultiplexer #(.select(5), .enable("false")) demultiplexer_1 (
    .out0(demultiplexer_1_out0), .out1(demultiplexer_1_out1), .out2(demultiplexer_1_out2),
    .out3(demultiplexer_1_out3), .out4(demultiplexer_1_out4), .out29(demultiplexer_1_out29),
    .out30(demultiplexer_1_out30), .in(WE), .sel(WA));  // open: out5, out6, out7, out8, out9, out10, out11, out12, out13, out14, out15, out16, out17, out18, out19, out20, out21, out22, out23, out24, out25, out26, out27, out28, out31
  Register #(.width(32)) register_3 (
    .D(in_3), .en(demultiplexer_1_out2), .Q(register_3_q), .clk(clock_1_out));  // open: clr
  Multiplexer #(.select(5), .width(32), .enable("false")) multiplexer_1 (
    .in0(register_1_q), .in1(register_2_q), .in2(register_3_q), .in3(register_4_q), .in4(r4_q),
    .in29(register_5_q), .in30(register_6_q), .in31({32{1'b0}}), .out(out_6), .sel(RA1));  // open: in5, in6, in7, in8, in9, in10, in11, in12, in13, in14, in15, in16, in17, in18, in19, in20, in21, in22, in23, in24, in25, in26, in27, in28
  Register #(.width(32)) register_4 (
    .D(in_3), .en(demultiplexer_1_out3), .Q(register_4_q), .clk(clock_1_out));  // open: clr
  Register #(.width(32)) r4 (.D(in_3), .en(demultiplexer_1_out4), .Q(r4_q), .clk(clock_1_out));  // open: clr
  Register #(.width(32)) register_5 (
    .D(in_3), .en(demultiplexer_1_out29), .Q(register_5_q), .clk(clock_1_out));  // open: clr
  Register #(.width(32)) register_6 (
    .D(in_3), .en(demultiplexer_1_out30), .Q(register_6_q), .clk(clock_1_out));  // open: clr
  Multiplexer #(.select(5), .width(32), .enable("false")) multiplexer_2 (
    .in0(register_1_q), .in1(register_2_q), .in2(register_3_q), .in3(register_4_q), .in4(r4_q),
    .in29(register_5_q), .in30(register_6_q), .in31({32{1'b0}}), .out(out_7), .sel(RA2));  // open: in5, in6, in7, in8, in9, in10, in11, in12, in13, in14, in15, in16, in17, in18, in19, in20, in21, in22, in23, in24, in25, in26, in27, in28

  // Notes on the sheet:
  //   r0
  //   r1
  //   r2
  //   RD1
  //   r3
  //   r29
  //   r30
  //   WD
  //   RD2
endmodule

module instruction_memory_x32 (
  input  [31:0] in_1,
  output [31:0] out_2
);

  ROM #(.dataWidth(32)) rom_1 (.addr(in_1[9:2]), .data(out_2));  // open: sel

  // Notes on the sheet:
  //   contents of rom_1 (hex, n*v repeats v):
  //   0 80611000 84611000 88611000 8c611000 c0610002 c4610002 c8610002 cc610002 a9611000 a4611000 a8611000
  //   e0610002 e4610002 e8610002 90611000 94611000 98611000 d0610002 d4610002 d8610002 b0611000 b4611000
  //   b8611000 f0610002 f4610002 f8610002
endmodule

module comparator_x32 (
  input  [31:0] in_1,
  input  [31:0] in_2,
  output [31:0] Greater,
  output [31:0] Equal,
  output [31:0] Smaller,
  output [31:0] Greater_or_equal,
  output [31:0] Lower_or_equal
);

  Comparator #(.width(32)) comparator_1 (.a(in_1), .b(in_2), .gt(Greater[0]), .eq(Equal[0]), .lt(Smaller[0]));
  or or_1 (Greater_or_equal[0], Greater[0], Equal[0]);
  or or_2 (Lower_or_equal[0], Smaller[0], Equal[0]);

  assign Equal[31:1] = {31{1'b0}};
  assign Greater[31:1] = {31{1'b0}};
  assign Greater_or_equal[31:1] = {31{1'b0}};
  assign Lower_or_equal[31:1] = {31{1'b0}};
  assign Smaller[31:1] = {31{1'b0}};
endmodule
